# Fritzing sketch Sketch_Probezusammenfassen (saved by Fritzing 0.9.3b)
breadboards: 1

parts:
  元件1 = Arduino Mega 2560 (Rev3)
  LCD1 = LCD screen
  R2 = Resistor [tolerance=±5% resistance=220 package=THT]
  R3 = Rotary Potentiometer (Small) [maximum_resistance=100kΩ package=THT]
  LED1 = LED - 5mm [color="Red (633nm)" package="5 mm [THT]"]
  LED2 = LED - 5mm [color="Red (633nm)" package="5 mm [THT]"]
  LED3 = LED - 5mm [color="Red (633nm)" package="5 mm [THT]"]
  R4 = Resistor [tolerance=±5% resistance=220 package=THT]
  R5 = Resistor [tolerance=±5% resistance=220 package=THT]
  R6 = Resistor [tolerance=±5% resistance=220 package=THT]
  S1 = Pushbutton [package="[THT]"]
  S2 = Pushbutton [package="[THT]"]
  S3 = Pushbutton [package="[THT]"]
  R7 = Resistor [tolerance=±5% resistance=220 package=THT]
  R9 = Resistor [tolerance=±5% resistance=220 package=THT]
  R10 = Resistor [tolerance=±5% resistance=220 package=THT]

nets:
  N1: 元件1.D8_PWM, S3.Pin_4, R9.Pin_1
  GND: 元件1.GND, LCD1.VSS, LCD1.R/W, LCD1.LED-, R2.Pin_1, R3.leg1, R4.Pin_1, R5.Pin_1, R6.Pin_1, S2.Pin_1, S2.Pin_2, S3.Pin_2, R7.Pin_1
  N2: 元件1.D2_PWM, LED1.cathode
  N3: 元件1.D3_PWM, LED2.cathode
  N4: 元件1.D4_PWM, LED3.cathode
  N5: 元件1.D6_PWM, S1.Pin_1, S1.Pin_2, R7.Pin_0
  N6: 元件1.D7_PWM, S2.Pin_3, S2.Pin_4, R10.Pin_1
  N7: 元件1.D35, LCD1.DB7
  N8: 元件1.D39, LCD1.DB6
  N9: 元件1.D43, LCD1.DB5
  N10: 元件1.D47, LCD1.DB4
  N11: 元件1.D51, LCD1.E
  N12: 元件1.D53, LCD1.RS
  N13: LCD1.VDD, R3.leg2, S1.Pin_3, S1.Pin_4, R9.Pin_0, R10.Pin_0
  N14: LCD1.V0, R3.wiper
  N15: LCD1.LED+, R2.Pin_0
  N16: LED1.anode, R4.Pin_0
  N17: LED2.anode, R5.Pin_0
  N18: LED3.anode, R6.Pin_0
