# Fritzing sketch Sketch_LCdisplay (saved by Fritzing 0.9.3b)
breadboards: 1

parts:
  元件1 = Arduino Mega 2560 (Rev3)
  LCD1 = LCD screen
  R1 = Rotary Potentiometer (Small) [maximum_resistance=100kΩ package=THT]
  R2 = Resistor [tolerance=±5% resistance=220 package=THT]

nets:
  N1: 元件1.D12_PWM, LCD1.RS
  N2: 元件1.D11_PWM, LCD1.E
  5V: 元件1.5V, LCD1.VDD, R1.leg2
  GND: 元件1.GND, LCD1.VSS, LCD1.R/W, LCD1.LED-, R1.leg1, R2.Pin_0
  N3: 元件1.D2_PWM, LCD1.DB7
  N4: 元件1.D3_PWM, LCD1.DB6
  N5: 元件1.D4_PWM, LCD1.DB5
  N6: 元件1.D5_PWM, LCD1.DB4
  N7: LCD1.V0, R1.wiper
  N8: LCD1.LED+, R2.Pin_1
